// Logisim project LAST LAB.circ as structural Verilog: 1 circuit, main circuit main
module main (
  input  DI0,
  input  DI1,
  input  DI2,
  input  DI3,
  input  E,
  input  [2:0] A,
  input  E_2,
  input  E_3,
  input  E_4,
  input  E_5,
  input  E_6,
  output DO0,
  output DO1,
  output DO2,
  output DO0_2,
  output DO1_2,
  output DO2_2,
  output DO3
);

  wire d_ff_1_q, d_ff_2_q, d_ff_3_q, d_ff_4_q, d_ff_5_q, d_ff_6_q, d_ff_7_q, d_ff_8_q, d_ff_9_q, d_ff_10_q,
       d_ff_11_q, d_ff_12_q, d_ff_13_q, d_ff_14_q, d_ff_15_q, d_ff_16_q, d_ff_17_q, d_ff_18_q, d_ff_19_q,
       d_ff_20_q, decoder_1_out0, decoder_1_out2, decoder_1_out4, decoder_1_out6, decoder_1_out7;

  Decoder #(.select(3)) decoder_1 (
    .out0(decoder_1_out0), .out2(decoder_1_out2), .out4(decoder_1_out4), .out6(decoder_1_out6),
    .out7(decoder_1_out7), .sel(A), .en(E_2));  // open: out1, out3, out5
  D_Flip_Flop #(.trigger("high")) d_ff_1 (
    .clk(decoder_1_out0), .D(DI0), .Q(d_ff_1_q), .en(E));  // open: Qn, preset, reset
  D_Flip_Flop #(.trigger("high")) d_ff_2 (
    .clk(decoder_1_out2), .D(DI0), .Q(d_ff_2_q), .en(E_3));  // open: Qn, preset, reset
  D_Flip_Flop #(.trigger("high")) d_ff_3 (
    .clk(decoder_1_out4), .D(DI0), .Q(d_ff_3_q), .en(E_4));  // open: Qn, preset, reset
  assign DO0 = decoder_1_out6 ? d_ff_4_q : 1'bz;  // Controlled_Buffer controlled_buffer_1
  D_Flip_Flop #(.trigger("high")) d_ff_4 (
    .clk(decoder_1_out6), .D(DI0), .Q(d_ff_4_q), .en(E_5));  // open: Qn, preset, reset
  D_Flip_Flop #(.trigger("high")) d_ff_5 (
    .clk(decoder_1_out7), .D(DI0), .Q(d_ff_5_q), .en(E_6));  // open: Qn, preset, reset
  assign DO0 = decoder_1_out7 ? d_ff_5_q : 1'bz;  // Controlled_Buffer controlled_buffer_2
  assign DO0 = decoder_1_out0 ? d_ff_1_q : 1'bz;  // Controlled_Buffer controlled_buffer_3
  assign DO0 = decoder_1_out2 ? d_ff_2_q : 1'bz;  // Controlled_Buffer controlled_buffer_4
  assign DO0 = decoder_1_out4 ? d_ff_3_q : 1'bz;  // Controlled_Buffer controlled_buffer_5
  D_Flip_Flop #(.trigger("high")) d_ff_6 (
    .clk(decoder_1_out0), .D(DI1), .Q(d_ff_6_q), .en(E));  // open: Qn, preset, reset
  D_Flip_Flop #(.trigger("high")) d_ff_7 (
    .clk(decoder_1_out2), .D(DI1), .Q(d_ff_7_q), .en(E_3));  // open: Qn, preset, reset
  D_Flip_Flop #(.trigger("high")) d_ff_8 (
    .clk(decoder_1_out4), .D(DI1), .Q(d_ff_8_q), .en(E_4));  // open: Qn, preset, reset
  D_Flip_Flop #(.trigger("high")) d_ff_9 (
    .clk(decoder_1_out6), .D(DI1), .Q(d_ff_9_q), .en(E_5));  // open: Qn, preset, reset
  D_Flip_Flop #(.trigger("high")) d_ff_10 (
    .clk(decoder_1_out7), .D(DI1), .Q(d_ff_10_q), .en(E_6));  // open: Qn, preset, reset
  assign DO1 = decoder_1_out0 ? d_ff_6_q : 1'bz;  // Controlled_Buffer controlled_buffer_6
  assign DO1 = decoder_1_out2 ? d_ff_7_q : 1'bz;  // Controlled_Buffer controlled_buffer_7
  assign DO1 = decoder_1_out4 ? d_ff_8_q : 1'bz;  // Controlled_Buffer controlled_buffer_8
  assign DO1 = decoder_1_out6 ? d_ff_9_q : 1'bz;  // Controlled_Buffer controlled_buffer_9
  assign DO1 = decoder_1_out7 ? d_ff_10_q : 1'bz;  // Controlled_Buffer controlled_buffer_10
  D_Flip_Flop #(.trigger("high")) d_ff_11 (
    .clk(decoder_1_out0), .D(DI2), .Q(d_ff_11_q), .en(E));  // open: Qn, preset, reset
  D_Flip_Flop #(.trigger("high")) d_ff_12 (
    .clk(decoder_1_out2), .D(DI2), .Q(d_ff_12_q), .en(E_3));  // open: Qn, preset, reset
  D_Flip_Flop #(.trigger("high")) d_ff_13 (
    .clk(decoder_1_out4), .D(DI2), .Q(d_ff_13_q), .en(E_4));  // open: Qn, preset, reset
  D_Flip_Flop #(.trigger("high")) d_ff_14 (
    .clk(decoder_1_out6), .D(DI2), .Q(d_ff_14_q), .en(E_5));  // open: Qn, preset, reset
  D_Flip_Flop #(.trigger("high")) d_ff_15 (
    .clk(decoder_1_out7), .D(DI2), .Q(d_ff_15_q), .en(E_6));  // open: Qn, preset, reset
  assign DO2 = decoder_1_out0 ? d_ff_11_q : 1'bz;  // Controlled_Buffer controlled_buffer_11
  assign DO2 = decoder_1_out2 ? d_ff_12_q : 1'bz;  // Controlled_Buffer controlled_buffer_12
  assign DO2 = decoder_1_out4 ? d_ff_13_q : 1'bz;  // Controlled_Buffer controlled_buffer_13
  assign DO2 = decoder_1_out6 ? d_ff_14_q : 1'bz;  // Controlled_Buffer controlled_buffer_14
  assign DO2 = decoder_1_out7 ? d_ff_15_q : 1'bz;  // Controlled_Buffer controlled_buffer_15
  D_Flip_Flop #(.trigger("high")) d_ff_16 (
    .clk(decoder_1_out0), .D(DI3), .Q(d_ff_16_q), .en(E));  // open: Qn, preset, reset
  D_Flip_Flop #(.trigger("high")) d_ff_17 (
    .clk(decoder_1_out2), .D(DI3), .Q(d_ff_17_q), .en(E_3));  // open: Qn, preset, reset
  D_Flip_Flop #(.trigger("high")) d_ff_18 (
    .clk(decoder_1_out4), .D(DI3), .Q(d_ff_18_q), .en(E_4));  // open: Qn, preset, reset
  D_Flip_Flop #(.trigger("high")) d_ff_19 (
    .clk(decoder_1_out6), .D(DI3), .Q(d_ff_19_q), .en(E_5));  // open: Qn, preset, reset
  D_Flip_Flop #(.trigger("high")) d_ff_20 (
    .clk(decoder_1_out7), .D(DI3), .Q(d_ff_20_q), .en(E_6));  // open: Qn, preset, reset
  assign DO3 = decoder_1_out0 ? d_ff_16_q : 1'bz;  // Controlled_Buffer controlled_buffer_16
  assign DO3 = decoder_1_out2 ? d_ff_17_q : 1'bz;  // Controlled_Buffer controlled_buffer_17
  assign DO3 = decoder_1_out4 ? d_ff_18_q : 1'bz;  // Controlled_Buffer controlled_buffer_18
  assign DO3 = decoder_1_out6 ? d_ff_19_q : 1'bz;  // Controlled_Buffer controlled_buffer_19
  assign DO3 = decoder_1_out7 ? d_ff_20_q : 1'bz;  // Controlled_Buffer controlled_buffer_20

  assign DO0_2 = DO0;
  assign DO1_2 = DO1;
  assign DO2_2 = DO2;
endmodule
