// Logisim project long gate.circ as structural Verilog: 1 circuit, main circuit main
module main (
  input  a_prime,
  input  b,
  input  b_prime,
  input  in_4,
  input  c,
  input  c_prime,
  input  a,
  input  b_2,
  input  c_2,
  output x
);

  wire and_1_out, and_2_out, and_3_out, and_4_out, not_1_out, not_2_out, not_3_out;

  not not_1 (not_1_out, a);
  not not_2 (not_2_out, b_2);
  not not_3 (not_3_out, c_2);
  and and_1 (and_1_out, not_1_out, not_2_out, c_2);
  and and_2 (and_2_out, not_1_out, not_2_out, not_3_out);
  and and_3 (and_3_out, a, not_2_out, not_3_out);
  and and_4 (and_4_out, a, not_2_out, c_2);
  or or_1 (x, and_1_out, and_2_out, and_3_out, and_4_out);

  // Notes on the sheet:
  //   a
endmodule
